# Fritzing sketch pra32-u-with-panel (saved by Fritzing 0.9.4)

parts:
  Pico1 = Raspberry Pi Pico
  SW0 = SWITCH-MOMENTARY-2 [package=tactile-pth-12mm]
  SW1 = SWITCH-MOMENTARY-2 [package=tactile-pth-12mm]
  SW2 = SWITCH-MOMENTARY-2 [package=tactile-pth-12mm]
  VR0 = Rotary Potentiometer (Small) [maximum_resistance=10kΩ package=THT]
  VR1 = Rotary Potentiometer (Small) [maximum_resistance=10kΩ package=THT]
  VR2 = Rotary Potentiometer (Small) [maximum_resistance=10kΩ package=THT]
  R0 = Resistor [tolerance=±5% resistance=10k package="2512 [SMD]"]
  R1 = Resistor [tolerance=±5% resistance=10k package="2512 [SMD]"]
  R2 = Resistor [tolerance=±5% resistance=10k package="2512 [SMD]"]

nets:
  DEBUG UART0 TX: Pico1.pin_1
  DEBUG UART0 RX: Pico1.pin_2
  N1: Pico1.pin_3, Pico1.pin_13, Pico1.pin_23, Pico1.pin_42, VR0.leg2, VR1.leg2, VR2.leg2, R0.Pin_1, R1.Pin_1, R2.Pin_1
  MIDI UART1 TX: Pico1.pin_6
  MIDI UART1 RX: Pico1.pin_7
  SSD1306 Compatible 128x64 OLED Display I2C1 SDA: Pico1.pin_9
  SSD1306 Compatible 128x64 OLED Display I2C1 SCL: Pico1.pin_10
  I2S DATA: Pico1.pin_12
  I2S BCLK: Pico1.pin_14
  I2S LRCLK: Pico1.pin_15
  N2: Pico1.pin_21, SW0.2, R0.Pin_0
  N3: Pico1.pin_24, SW1.2, R1.Pin_0
  N4: Pico1.pin_26, SW2.2, R2.Pin_0
  I2S DAC MUTE OFF: Pico1.pin_29
  N5: Pico1.pin_31, VR0.wiper
  N6: Pico1.pin_32, VR1.wiper
  N7: Pico1.pin_34, VR2.wiper
  N8: Pico1.pin_36, SW0.1, SW1.1, SW2.1, VR0.leg1, VR1.leg1, VR2.leg1

custom parts:
  Raspberry Pi Pico: Raspberry Pi Pico. Based around the RP2040 microcontroller the Pico is a low cost microcontroller device bringing Raspberry Pi quality, cost, and easy of use to the microcontroller space. Jan 2021, Split part in to two versions: tht (this one) and SMD. This one will drill holes for a .1 in header in pcb to allow plugging in the module as well as providing pads to solder the module to the top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
