# Fritzing sketch pra32-u2-pwm-audio (saved by Fritzing 0.9.4)
breadboards: 1

parts:
  P1 = Raspberry Pi Pico
  U1 = 3.5mm Audio Jack [package=audio-jack-3.5mm-smd]
  R1 = Resistor [tolerance=±5% resistance=220 package="0402 [SMD]"]
  R2 = Resistor [tolerance=±5% resistance=220 package="0402 [SMD]"]
  C1 = Ceramic Capacitor [capacitance="100 nF" package="0603 [SMD, multilayer]"]
  C2 = Ceramic Capacitor [capacitance="100 nF" package="0603 [SMD, multilayer]"]

nets:
  N1: P1.pin_3, P1.pin_8, P1.pin_13, P1.pin_18, P1.pin_23, P1.pin_28, P1.pin_33, P1.pin_38, U1.SLEEVE, C1.0, C2.0
  N2: P1.pin_32, R2.Pin_0
  N3: P1.pin_34, R1.Pin_0
  N4: U1.RIGHT, R2.Pin_1, C2.1
  N5: U1.LEFT, R1.Pin_1, C1.1

custom parts:
  Raspberry Pi Pico: Raspberry Pi Pico. Based around the RP2040 microcontroller the Pico is a low cost microcontroller device bringing Raspberry Pi quality, cost, and easy of use to the microcontroller space. Jan 2021, Split part in to two versions: tht (this one) and SMD. This one will drill holes for a .1 in header in pcb to allow plugging in the module as well as providing pads to solder the module to the top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
