# Fritzing sketch pra32-u2-with-panel-8 (saved by Fritzing 0.9.4)

parts:
  Pico = Raspberry Pi Pico
  SW0 = SWITCH-MOMENTARY-2 [package=tactile-pth-12mm]
  SW1 = SWITCH-MOMENTARY-2 [package=tactile-pth-12mm]
  SW2 = SWITCH-MOMENTARY-2 [package=tactile-pth-12mm]
  VR0 = Rotary Potentiometer (Small) [maximum_resistance=10kΩ package=THT]
  VR1 = Rotary Potentiometer (Small) [maximum_resistance=10kΩ package=THT]
  VR2 = Rotary Potentiometer (Small) [maximum_resistance=10kΩ package=THT]
  SW3_(Optional) = SWITCH-MOMENTARY-2 [package=tactile-pth-12mm]
  SW4_(Optional) = SWITCH-MOMENTARY-2 [package=tactile-pth-12mm]
  SW5_(Optional) = SWITCH-MOMENTARY-2 [package=tactile-pth-12mm]

nets:
  DEBUG (UART0 TX): Pico.pin_1
  DEBUG (UART0 RX): Pico.pin_2
  MIDI (UART1 TX): Pico.pin_6
  MIDI (UART1 RX): Pico.pin_7
  SSD1306 based 128x64 OLED (I2C1 SDA): Pico.pin_9
  SSD1306 based 128x64 OLED (I2C1 SCL): Pico.pin_10
  I2S DATA (DIN): Pico.pin_12
  I2S MCLK (MCK, SCK): Pico.pin_13, Pico.pin_42, SW0.2, VR0.leg2, VR1.leg2, VR2.leg2, SW3_(Optional).2
  I2S BCLK (BCK): Pico.pin_14
  I2S LRCLK (LRCK, LCK, WCK, WSEL): Pico.pin_15
  N1: Pico.pin_21, SW0.1
  N2: Pico.pin_22, SW3_(Optional).1
  N3: Pico.pin_24, SW1.1
  N4: Pico.pin_25, SW4_(Optional).1
  N5: Pico.pin_26, SW2.1
  N6: Pico.pin_27, SW5_(Optional).1
  I2S DAC MUTE OFF (XSMT) (Optional): Pico.pin_29
  N7: Pico.pin_31, VR0.wiper
  N8: Pico.pin_32, VR1.wiper
  N9: Pico.pin_34, VR2.wiper
  N10: Pico.pin_36, VR0.leg1, VR1.leg1, VR2.leg1
  Adafruit PCM510x I2S DAC VIN/GY-PCM5102 VIN/SSD1306 based 128x64 OLED VCC: Pico.pin_40
  N11: SW1.2, SW4_(Optional).2
  N12: SW2.2, SW5_(Optional).2

custom parts:
  Raspberry Pi Pico: Raspberry Pi Pico. Based around the RP2040 microcontroller the Pico is a low cost microcontroller device bringing Raspberry Pi quality, cost, and easy of use to the microcontroller space. Jan 2021, Split part in to two versions: tht (this one) and SMD. This one will drill holes for a .1 in header in pcb to allow plugging in the module as well as providing pads to solder the module to the top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
