# Fritzing sketch vra8-nx-circuit-diagram (saved by Fritzing 0.9.4)
breadboards: 1

parts:
  A1 = Arduino Uno (Rev3)
  R1 = Resistor [tolerance=±5% resistance=220 package="2512 [SMD]"]
  U1 = 3.5mm Audio Jack [package=audio-jack-3.5mm-smd]
  C1 = Ceramic Capacitor [capacitance=100nF package="200 mil [THT, multilayer]"]

nets:
  N1: A1.GND, U1.RIGHT, U1.SLEEVE, C1.0
  N2: A1.D5_PWM, R1.Pin_0
  N3: R1.Pin_1, U1.LEFT, C1.1
