# Fritzing sketch vra8-q-2nd-order-post-lpf-ac-coupling-circuit-diagram (saved by Fritzing 0.9.4)
breadboards: 1

parts:
  A1 = Arduino Uno (Rev3)
  R1 = Resistor [tolerance=±5% resistance=47 package="2512 [SMD]"]
  R2 = Resistor [tolerance=±5% resistance=47 package="2512 [SMD]"]
  R4 = Resistor [tolerance=±5% resistance=47 package="2512 [SMD]"]
  R5 = Resistor [tolerance=±5% resistance=47 package="2512 [SMD]"]
  U1 = 3.5mm Audio Jack [package=audio-jack-3.5mm-smd]
  C1 = Ceramic Capacitor [capacitance=100nF package="200 mil [THT, multilayer]"]
  C2 = Ceramic Capacitor [capacitance=100nF package="200 mil [THT, multilayer]"]
  C5 = Ceramic Capacitor [capacitance=100nF package="200 mil [THT, multilayer]"]
  C4 = Ceramic Capacitor [capacitance=100nF package="200 mil [THT, multilayer]"]
  C3_10uF = Capacitor Polarized [package=cpol-radial-10uf-25v]
  C6_10uF = Capacitor Polarized [package=cpol-radial-10uf-25v]
  R3 = Resistor [tolerance=±5% resistance=47 package="2512 [SMD]"]
  R6 = Resistor [tolerance=±5% resistance=47 package="2512 [SMD]"]

nets:
  N1: A1.D11_PWM/MOSI, R4.Pin_0
  N2: A1.GND, U1.SLEEVE, C1.0, C2.0, C5.0, C4.0
  N3: A1.D5_PWM, R1.Pin_0
  N4: R1.Pin_1, R2.Pin_0, C1.1
  N5: R2.Pin_1, C2.1, R3.Pin_0
  N6: R4.Pin_1, R5.Pin_0, C4.1
  N7: R5.Pin_1, C5.1, R6.Pin_0
  N8: U1.RIGHT, C6_10uF.-
  N9: U1.LEFT, C3_10uF.-
  N10: C3_10uF.+, R3.Pin_1
  N11: C6_10uF.+, R6.Pin_1
