# Fritzing sketch vra8-q-2nd-order-post-lpf-bread-board (saved by Fritzing 0.9.4)
breadboards: 1

parts:
  A1 = Arduino Uno (Rev3)
  R1 = Resistor [tolerance=±5% resistance=47 package="2512 [SMD]"]
  R2 = Resistor [tolerance=±5% resistance=47 package="2512 [SMD]"]
  R3 = Resistor [tolerance=±5% resistance=47 package="2512 [SMD]"]
  R4 = Resistor [tolerance=±5% resistance=47 package="2512 [SMD]"]
  R5 = Resistor [tolerance=±5% resistance=47 package="2512 [SMD]"]
  R6 = Resistor [tolerance=±5% resistance=47 package="2512 [SMD]"]
  U1 = 3.5mm Audio Jack [package=audio-jack-3.5mm-smd]
  C1 = Film/Foil Capacitor [capacitance=100nF voltage=35V package="7.5mm [THT, pp]"]
  C2 = Film/Foil Capacitor [capacitance=100nF voltage=35V package="7.5mm [THT, pp]"]
  C3 = Film/Foil Capacitor [capacitance=100nF voltage=35V package="7.5mm [THT, pp]"]
  C4 = Film/Foil Capacitor [capacitance=100nF voltage=35V package="7.5mm [THT, pp]"]

nets:
  N1: A1.D11_PWM/MOSI, R4.Pin_0
  N2: A1.GND, U1.SLEEVE, C1.-, C2.-
  N3: A1.D5_PWM, R1.Pin_0
  N4: R1.Pin_1, R2.Pin_0, C1.+
  N5: R2.Pin_1, R3.Pin_0, C2.+
  N6: R3.Pin_1, U1.LEFT
  N7: R4.Pin_1, R5.Pin_0, C3.-
  N8: R5.Pin_1, R6.Pin_0, C4.-
  N9: R6.Pin_1, U1.RIGHT
  N10: C3.+, C4.+
