# Fritzing sketch vra8-u-bread-board (saved by Fritzing 0.9.4)
breadboards: 1

parts:
  A1 = Arduino Uno (Rev3)
  R1 = Resistor [tolerance=±5% resistance=220 package="2512 [SMD]"]
  R4 = Resistor [tolerance=±5% resistance=220 package="2512 [SMD]"]
  U1 = 3.5mm Audio Jack [package=audio-jack-3.5mm-smd]
  C4 = Ceramic Capacitor [capacitance=100nF package="100 mil [THT, multilayer]"]
  C5 = Ceramic Capacitor [capacitance=100nF package="100 mil [THT, multilayer]"]

nets:
  N1: A1.D11_PWM/MOSI, R4.Pin_0
  N2: A1.GND, U1.SLEEVE, C4.0, C5.1
  N3: A1.D5_PWM, R1.Pin_0
  N4: R1.Pin_1, U1.LEFT, C4.1
  N5: R4.Pin_1, U1.RIGHT, C5.0
