# Fritzing sketch vra8-u-type-16 (saved by Fritzing 0.9.4)
breadboards: 1

parts:
  A1 = Arduino Uno (Rev3)
  R1 = Resistor [tolerance=±5% resistance=220 package="2512 [SMD]"]
  R2 = Resistor [tolerance=±5% resistance=220 package="2512 [SMD]"]
  U1 = 3.5mm Audio Jack [package=audio-jack-3.5mm-smd]
  C1 = Ceramic Capacitor [capacitance=100nF package="100 mil [THT, multilayer]"]
  C4_10uF = Capacitor Polarized [package=cpol-radial-10uf-25v]
  C3_10uF = Capacitor Polarized [package=cpol-radial-10uf-25v]
  R3 = Resistor [tolerance=±5% resistance=56k package="2512 [SMD]"]
  C2 = Ceramic Capacitor [capacitance=100nF package="100 mil [THT, multilayer]"]
  R4 = Resistor [tolerance=±5% resistance=56k package="2512 [SMD]"]

nets:
  N1: A1.D11_PWM/MOSI, R2.Pin_0
  N2: A1.GND, U1.SLEEVE, C1.0, C2.0
  N3: A1.D3_PWM, R4.Pin_0
  N4: A1.D5_PWM, R1.Pin_0
  N5: A1.D6_PWM, R3.Pin_0
  N6: R1.Pin_1, C1.1, C3_10uF.+, R3.Pin_1
  N7: R2.Pin_1, C4_10uF.+, C2.1, R4.Pin_1
  N8: U1.RIGHT, C4_10uF.-
  N9: U1.LEFT, C3_10uF.-
